# Fritzing sketch rpm_generator (saved by Fritzing 0.9.3b)
breadboards: 1

parts:
  U1 = NodeMCU V3.0
  U2 = LM2596 step down module
  R1 = Rotary Potentiometer (Small) [maximum_resistance=100kΩ package=THT]

nets:
  N1: U1.GND#6, U1.GND#13, U1.GND#16, U1.GND#33, U2.IN-, U2.OUT-, R1.leg1
  N2: U1.Vin, U2.OUT+, R1.leg2
  N3: U1.A0, R1.wiper

notes:
  RPM 訊號產生器 (直流)
  https://3wa.tw
  By 羽山秋人
  2021-09-06
  VCC 12V
  GND
  LM2596
  VR B10K
  Nodemcu V2
  A0
  D1
  輸出 RPM 轉速訊號

custom parts:
  NodeMCU V3.0: ESP8266 based NodeMCU
  LM2596 step down module: LM2596 DC-DC step down power supply module 3 A.
