# Fritzing sketch rpm_generator_ac (saved by Fritzing 0.9.3b)
breadboards: 1

parts:
  U1 = NodeMCU V3.0
  U2 = LM2596 step down module
  R1 = Rotary Potentiometer (Small) [maximum_resistance=100kΩ package=THT]
  Q1 = NPN-Transistor [package="TO92 [THT]"]
  R2 = Resistor [tolerance=±5% resistance=4.7k package=THT]
  Q3 = pnp-Powertransistor [package="TO220 [THT]"]
  Q2 = npn-Powertransistor [package="TO220 [THT]"]
  R3 = Resistor [tolerance=±5% resistance=2.2k package=THT]
  R4 = Resistor [tolerance=±5% resistance=2.2k package=THT]
  U3 = Transformer [package=transformer]

nets:
  N1: U1.D1, Q1.B
  N2: U1.GND#6, U1.GND#13, U1.GND#16, U1.GND#33, R1.leg1, R4.Pin_1, U3.2, U3.3
  N3: U1.Vin, U2.OUT+, R1.leg2
  N4: U1.A0, R1.wiper
  N5: U2.IN-, U2.OUT-
  N6: Q1.E, Q3.base, Q2.base
  N7: Q1.C, R2.Pin_1
  N8: R2.Pin_0, R3.Pin_0
  N9: Q3.collector, R4.Pin_0
  N10: Q3.emitter, Q2.emitter, U3.5
  N11: Q2.collector, R3.Pin_1

notes:
  RPM 訊號產生器 (交流)
  https://3wa.tw
  By 羽山秋人
  2021-09-06
  VCC 12V
  GND
  LM2596
  VR B10K
  Nodemcu V2
  A0
  D1
  輸出 RPM 轉速訊號
  C945
  TIP41C
  TIP42C
  1:3 變壓器

custom parts:
  NodeMCU V3.0: ESP8266 based NodeMCU
  LM2596 step down module: LM2596 DC-DC step down power supply module 3 A.
  Transformer: Small transformers
